# Fritzing sketch Circuitry (saved by Fritzing 0.9.3b)

parts:
  U1 = ESP32S-HiLetgo [part_number=ESP32S-HiLetgo]
  Grove1 = Grove OLED 128x96
  Mod1 = KY-032 IR Obstacle Avoidance Sensor Module [package="Breakout board"]
  J1 = Basic Servo
  Εξάρτημα1 = Arduino Uno (Rev3)
  L298N1 = L298N DC motor driver
  VCC1 = Battery block 9V
  M1 = DC Motor
  S1 = Pushbutton [package="[SMD]"]
  S2 = Pushbutton [package="[SMD]"]
  S3 = Pushbutton [package="[SMD]"]

nets:
  N1: U1.3.3, Grove1.VCC, Mod1.EN
  N2: U1.EN, Mod1.out
  N3: U1.GPIO32, S2.Pin_2
  N4: U1.GPIO33, S2.Pin_4
  N5: U1.GPIO27, L298N1.IN2
  N6: U1.GPIO14, L298N1.IN1
  N7: U1.GPIO12, L298N1.ENA
  GND: U1.GND, Grove1.GND, Mod1.GND, J1.gnd, Εξάρτημα1.GND, L298N1.GND, VCC1.-
  N8: U1.GPIO13, J1.pulse
  N9: U1.GPIO15, S1.Pin_3, S1.Pin_4
  N10: U1.GPIO2, S1.Pin_1, S1.Pin_2
  N11: U1.GPIO0, S3.Pin_3, S3.Pin_4
  N12: U1.GPIO4, S3.Pin_1, S3.Pin_2
  N13: U1.GPIO16, Εξάρτημα1.D1/TX
  N14: U1.GPIO17, Εξάρτημα1.D0/RX
  N15: U1.GPIO21, Grove1.SDA
  N16: U1.GPIO22, Grove1.SCL
  VCC: J1.vcc, Εξάρτημα1.VIN, L298N1.5V
  N17: L298N1.OUT1, M1.pin_1
  N18: L298N1.OUT2, M1.pin_2
  N19: L298N1.12V, VCC1.+

notes:
  Jetson Nano
  Oled screen
  Color Sensor
  ESP-32
  12V Battery
  L298N Accelerometer
  Servo Motor
  EV3 Lego Servo Motor
  BUTTONS

custom parts:
  ESP32S-HiLetgo: HiLetgo ESP-WROOM-32 ESP32 ESP-32S Development Board 2.4GHz Dual-Mode WiFi + Bluetooth Dual Cores Microcontroller The ESP32 integrated with Antenna switches, RF Balun, power amplifiers, low-noise amplifiers, filters, and management modules, and the entire solution occupies the least area of PCB. 2.4 GHz Wi-Fi plus Bluetooth dual-mode chip, with TSMC Ultra-low power consumption 40nm technology,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
  KY-032 IR Obstacle Avoidance Sensor Module: KY-032 Infrared Obstacle Avoidance Sensor. Distance-adjustable, infrared proximity sensor designed for wheeled robots. Also known as AD-032.
  L298N DC motor driver: 2x DC motor driver with 78M05 positive voltage regulator (7..35 V) L298N: max 46 V, 2 A Set 5 V Enable jumper to enable 5 V regultor (needed for the L298N) and +5 V output at screw terminal or supply external +5 V at screw terminal Set ENA and/or ENB to +5 V to enable motor permanently or supply ENA and/or ENB with PWM signal IN1 and IN2 set rotation directory for motor A (OUT1/OUT2) IN2 and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
